// Logisim project circuito_simplified.circ as structural Verilog: 4 circuits, main circuit main
module main (
  input  \Botão ,
  input  Sensor_porta_aberta,
  input  Sensor_roupa_seca,
  input  Sensor_temperatura,
  output Rodar_para_a_direita,
  output Rodar_para_a_esquerda,
  output Elemento_de_aquecimento
);

  wire and_1_out, or_1_out;

  or or_1 (or_1_out, Sensor_porta_aberta, Sensor_roupa_seca);
  and and_1 (and_1_out, \Botão , ~or_1_out, ~Sensor_temperatura);  // AND_Gate
  MCMA \Módulo_controlo_máquina  (
    .Bi___SPA_SRS___ST(and_1_out), .RD(Rodar_para_a_direita), .RE(Rodar_para_a_esquerda),
    .EA(Elemento_de_aquecimento));
endmodule

module MCMO02 (
  input  OK__SSBi,
  output RD,
  output RE
);

  wire A_q, A_qn, and_1_out, and_2_out, and_3_out, and_4_out, B_q, C_q, CLK_out, or_1_out;

  and and_1 (and_1_out, OK__SSBi, B_q, C_q);
  and and_2 (and_2_out, OK__SSBi, C_q);
  or or_1 (or_1_out, ~OK__SSBi, C_q);  // OR_Gate
  and and_3 (and_3_out, OK__SSBi, A_qn);
  xor xor_1 (RD, B_q, C_q);
  and and_4 (and_4_out, B_q, C_q);
  or or_2 (RE, and_4_out, A_q);
  Clock CLK (.out(CLK_out));
  J_K_Flip_Flop A (.J(and_1_out), .clk(CLK_out), .K(1'b1), .Q(A_q), .Qn(A_qn));  // open: preset, en, reset
  J_K_Flip_Flop B (.J(and_2_out), .clk(CLK_out), .K(or_1_out), .Q(B_q));  // open: Qn, preset, en, reset
  J_K_Flip_Flop C (.J(and_3_out), .clk(CLK_out), .K(1'b1), .Q(C_q));  // open: Qn, preset, en, reset
endmodule

module MCT (
  input  OK___ST___SSBi,
  output out_2
);

  wire clock_1_out, not_1_out;

  Clock clock_1 (.out(clock_1_out));
  not not_1 (not_1_out, OK___ST___SSBi);
  J_K_Flip_Flop j_k_ff_1 (
    .J(OK___ST___SSBi), .clk(clock_1_out), .K(not_1_out), .Q(out_2));  // open: Qn, preset, en, reset
endmodule

module MCMA (
  input  Bi___SPA_SRS___ST,
  output RD,
  output RE,
  output EA
);

  wire clock_1_out, j_k_ff_1_q, not_1_out;

  Clock clock_1 (.out(clock_1_out));
  not not_1 (not_1_out, Bi___SPA_SRS___ST);
  J_K_Flip_Flop j_k_ff_1 (
    .J(Bi___SPA_SRS___ST), .clk(clock_1_out), .K(not_1_out), .Q(j_k_ff_1_q));  // open: Qn, preset, en, reset
  MCMO02 MCMO (.OK__SSBi(j_k_ff_1_q), .RD(RD), .RE(RE));
  MCT MCT (.OK___ST___SSBi(j_k_ff_1_q), .out_2(EA));
endmodule
